// Digital circuit baby8_control.dig as structural Verilog
module baby8_control (
  input  [7:0] R,
  input  Z,
  input  C,
  input  N,
  input  V,
  input  clock,
  input  resetn,
  input  \int ,
  output wReg,
  output [3:0] wAd,
  output [3:0] aAd,
  output [3:0] bAd,
  output [1:0] bSel,
  output [1:0] logSel,
  output [1:0] aSel,
  output Cin,
  output A7,
  output A0,
  output a7S,
  output a0S,
  output wMem,
  output out3,
  output out2,
  output out1,
  output out0
);

  Register #(.Bits(8)) IR (.D(R), .C(clock));  // open: en, Q
  Register #(.Bits(4)) flags (.D({V, N, C, Z}), .C(clock));  // open: en, Q
endmodule
