// Digital circuit baby8cpu.dig as structural Verilog
module baby8cpu (
);

  baby8_datapath baby8_datapath_1 ();  // open: clock, in0, in1, wReg, wAd, aAd, bAd, dIn, bSel, logSel, aSel, Cin, A7, A0, a7S, a0S, R, dOut, address, Z, C, N, V
endmodule
